// Logisim project lab4.circ as structural Verilog: 6 circuits, main circuit main
module main (
  input  R,
  input  S,
  output out_3,
  output out_4
);

  nor nor_1 (out_3, R, out_4);
  nor nor_2 (out_4, out_3, S);
endmodule

module \схема_2  (
  input  S,
  input  R,
  output out_3,
  output out_4
);

  nand nand_1 (out_3, S, out_4);
  nand nand_2 (out_4, out_3, R);
endmodule

module \Схема_3  (
  input  S,
  input  C,
  input  R,
  output out_4,
  output out_5
);

  wire nand_1_out, nand_2_out;

  nand nand_1 (nand_1_out, S, C);
  nand nand_2 (nand_2_out, C, R);
  nand nand_3 (out_4, nand_1_out, out_5);
  nand nand_4 (out_5, out_4, nand_2_out);
endmodule

module \Схема_4  (
  input  S,
  input  R,
  output out_3,
  output out_4
);

  wire nand_1_out, nand_2_out;

  nand nand_1 (nand_1_out, S, S);
  nand nand_2 (nand_2_out, nand_1_out, R);
  nand nand_3 (out_3, nand_1_out, out_4);
  nand nand_4 (out_4, out_3, nand_2_out);
endmodule

module \Схема_5  (
  input  S,
  input  R,
  output out_3,
  output out_4
);

  wire nand_1_out, nand_2_out;

  nand nand_1 (nand_1_out, S, nand_2_out);
  nand nand_2 (nand_2_out, R, R);
  nand nand_3 (out_3, nand_1_out, out_4);
  nand nand_4 (out_4, out_3, nand_2_out);
endmodule

module \Схема_6  (
  input  S,
  input  R,
  output out_3,
  output out_4
);

  wire nand_1_out, nand_2_out, nand_3_out, nand_4_out, undriven;

  nand nand_1 (nand_1_out, S, S);
  nand nand_2 (nand_2_out, R, R);
  nand nand_3 (nand_3_out, S, nand_2_out);
  nand nand_4 (nand_4_out, nand_1_out, R);
  nand nand_5 (out_3, nand_3_out, undriven);
  nand nand_6 (out_4, out_3, nand_4_out);
endmodule
